// Digital circuit cpu.dig as structural Verilog
module cpu (
  input  [15:0] MemIn,
  input  MemReady,
  input  Clk,
  output [15:0] MemAddr,
  output [15:0] MemOut
);

  wire register_1_q;

  Register register_1 (.D(MemIn[0]), .C(Clk), .en(MemReady), .Q(register_1_q));
  // Pins of 1 and 16 bits meet at MemIn
endmodule
